# Fritzing sketch Skecth_pertanian (saved by Fritzing 0.9.3b)
breadboards: 1

parts:
  LCD1 = LCD screen
  LCM1602_IIC1 = LCM1602 IIC [part_number="LCM1602 IIC" chip_label="LCM1602 IIC" package="DIP (Dual Inline) [THT]"]
  A1 = Arduino UNO R4 WiFi
  Capacitive_Soil_Moisture_Sensor1 = Capacitive Soil Moisture Sensor V2.0
  YL-83_-_Detection_Board1 = YL-83 Rain Sensor - Detection Board
  WATER_PUMP1 = water pump/motor
  Part2 = MQ-9 breakout
  M1 = 1 chan 5v relay module
  YL-83_-_Control_Board1 = YL-83 Rain Sensor - Control Board
  e-radionica_com1 = LM393 LDR breakout [part_number=100027]
  DHT11_1 = DHT11 module

nets:
  VSS: LCD1.VSS, LCM1602_IIC1.VSS
  VDD: LCD1.VDD, LCM1602_IIC1.VDD
  N1: LCD1.V0, LCM1602_IIC1.V0
  N2: LCD1.RS, LCM1602_IIC1.RS
  N3: LCD1.R/W, LCM1602_IIC1.RW
  N4: LCD1.E, LCM1602_IIC1.E
  N5: LCD1.DB0, LCM1602_IIC1.D0
  N6: LCD1.DB1, LCM1602_IIC1.D1
  N7: LCD1.DB2, LCM1602_IIC1.D2
  N8: LCD1.DB3, LCM1602_IIC1.D3
  N9: LCD1.DB4, LCM1602_IIC1.D4
  N10: LCD1.DB5, LCM1602_IIC1.D5
  N11: LCD1.DB6, LCM1602_IIC1.D6
  N12: LCD1.DB7, LCM1602_IIC1.D7
  N13: LCD1.LED+, LCM1602_IIC1.A
  N14: LCD1.LED-, LCM1602_IIC1.K
  GND: LCM1602_IIC1.GND, A1.Pin_2, A1.Pin_9, A1.Pin_18, A1.Pin_48, Capacitive_Soil_Moisture_Sensor1.GND, Part2.GND, M1.pin_2, M1.pin_5, YL-83_-_Control_Board1.GND, e-radionica_com1.GND, DHT11_1.GND
  VCC: LCM1602_IIC1.VCC, A1.Pin_8, A1.Pin_27, Capacitive_Soil_Moisture_Sensor1.VCC, WATER_PUMP1.pin_2, Part2.VCC, M1.pin_1, YL-83_-_Control_Board1.VCC, e-radionica_com1.DO, DHT11_1.VCC
  N15: LCM1602_IIC1.SDA, A1.Pin_16
  N16: LCM1602_IIC1.SCL, A1.Pin_17
  N17: A1.Pin_12, Capacitive_Soil_Moisture_Sensor1.AOUT
  N18: A1.Pin_13, Part2.AO
  N19: A1.Pin_14, e-radionica_com1.AO
  N20: A1.Pin_15, YL-83_-_Control_Board1.AO
  N21: A1.Pin_36, M1.pin_3
  N22: A1.Pin_41, DHT11_1.DATA
  N23: YL-83_-_Detection_Board1.POS, YL-83_-_Control_Board1.NEG
  N24: YL-83_-_Detection_Board1.NEG, YL-83_-_Control_Board1.POS
  N25: WATER_PUMP1.pin_1, M1.pin_4

notes:
  Light Sensor
  Air Quality Sensor
  Raindrop Sensor
  Soil Moisture Sensor
  Temperature & Humidity Sensor
  Water Pump
  One Channel Relay 5V
  LCD Display 16x2
  I2C Converter 16 to 4 pin
  (MQ-135)
  (DHT11)
  (LDR)

custom parts:
  LCM1602 IIC: I2C-Module to use a 1602 or 2004 LCD on with the wire.h libory Serial LCD Modul
  Arduino UNO R4 WiFi: The Arduino UNO R4 WiFi merges the RA4M1 microprocessor from Renesas with the ESP32-S3 from Espressif, creating an all-in-one tool for makers with enhanced processing power and a diverse array of new peripherals.
  YL-83 Rain Sensor - Detection Board: The YL-83 is a rain sensor that has more resistance when dry and less resistance when wet. The module runs at 5V.
  water pump/motor: WATER PUMP BY ARDUBLOCKTR
  MQ-9 breakout: SKU: 101284
  1 chan 5v relay module: 1 Channel 5V Relay Module Board Shield with Optocoupler Support High and Low Level Trigger for Arduino.
  YL-83 Rain Sensor - Control Board: The YL-83 is a rain sensor that has more resistance when dry and less resistance when wet. The module runs at 5V.
  DHT11 module: https://cdn-learn.adafruit.com/downloads/pdf/dht.pdf DHT11 black pcb module reference by:https://github.com/adafruit/Fritzing-Library/blob/master/parts/DHT11%20Humitidy%20and%20Temperature%20Sensor.fzpz
